// Logisim project CSE332_Rahiq_Tazrian.circ as structural Verilog
module _1_bit_ALU (
  input  A,
  input  B,
  input  CarryIn,
  input  [1:0] S1S0,
  output Result,
  output Cout
);

  wire adder_1_out, and_1_out, and_2_out, multiplexer_1_out, not_1_out, or_1_out;

  Multiplexer #(.enable("false")) multiplexer_1 (.in0(B), .in1(not_1_out), .out(multiplexer_1_out), .sel(and_1_out));
  not not_1 (not_1_out, B);
  and and_1 (and_1_out, S1S0[0], S1S0[1]);
  and and_2 (and_2_out, A, B);
  or or_1 (or_1_out, A, B);
  Adder #(.width(1)) adder_1 (.a(A), .b(multiplexer_1_out), .out(adder_1_out), .cin(CarryIn), .cout(Cout));
  Multiplexer #(.select(2), .enable("false")) multiplexer_2 (
    .in0(and_2_out), .in1(or_1_out), .in2(adder_1_out), .in3(adder_1_out), .out(Result), .sel(S1S0));
endmodule

module _32_bit_ALU (
  input  CarryIn,
  input  in_2,
  input  [31:0] A,
  input  [1:0] ALU_Operation,
  input  [31:0] B,
  output [31:0] Result,
  output Overflow,
  output Zero,
  output out_9
);

  wire and_1_out, multiplexer_1_out, n1_bit_alu_1_cout, n1_bit_alu_2_cout, n1_bit_alu_3_cout,
       n1_bit_alu_4_cout, n1_bit_alu_5_cout, n1_bit_alu_6_cout, n1_bit_alu_7_cout, n1_bit_alu_8_cout,
       n1_bit_alu_9_cout, n1_bit_alu_10_cout, n1_bit_alu_11_cout, n1_bit_alu_12_cout, n1_bit_alu_13_cout,
       n1_bit_alu_14_cout, n1_bit_alu_15_cout, n1_bit_alu_16_cout, n1_bit_alu_17_cout, n1_bit_alu_18_cout,
       n1_bit_alu_19_cout, n1_bit_alu_20_cout, n1_bit_alu_21_cout, n1_bit_alu_22_cout, n1_bit_alu_23_cout,
       n1_bit_alu_24_cout, n1_bit_alu_25_cout, n1_bit_alu_26_cout, n1_bit_alu_27_cout, n1_bit_alu_28_cout,
       n1_bit_alu_29_cout, n1_bit_alu_30_cout, n1_bit_alu_31_cout;

  Multiplexer #(.enable("false")) multiplexer_1 (.in0(CarryIn), .in1(in_2), .out(multiplexer_1_out), .sel(and_1_out));
  and and_1 (and_1_out, ALU_Operation[0], ALU_Operation[1]);
  _1_bit_ALU u_1_bit_alu_1 (
    .A(A[0]), .B(B[0]), .CarryIn(multiplexer_1_out), .S1S0(ALU_Operation), .Result(Result[0]),
    .Cout(n1_bit_alu_1_cout));
  _1_bit_ALU u_1_bit_alu_2 (
    .A(A[1]), .B(B[1]), .CarryIn(n1_bit_alu_1_cout), .S1S0(ALU_Operation), .Result(Result[1]),
    .Cout(n1_bit_alu_2_cout));
  _1_bit_ALU u_1_bit_alu_3 (
    .A(A[2]), .B(B[2]), .CarryIn(n1_bit_alu_2_cout), .S1S0(ALU_Operation), .Result(Result[2]),
    .Cout(n1_bit_alu_3_cout));
  _1_bit_ALU u_1_bit_alu_4 (
    .A(A[3]), .B(B[3]), .CarryIn(n1_bit_alu_3_cout), .S1S0(ALU_Operation), .Result(Result[3]),
    .Cout(n1_bit_alu_4_cout));
  _1_bit_ALU u_1_bit_alu_5 (
    .A(A[4]), .B(B[4]), .CarryIn(n1_bit_alu_4_cout), .S1S0(ALU_Operation), .Result(Result[4]),
    .Cout(n1_bit_alu_5_cout));
  _1_bit_ALU u_1_bit_alu_6 (
    .A(A[5]), .B(B[5]), .CarryIn(n1_bit_alu_5_cout), .S1S0(ALU_Operation), .Result(Result[5]),
    .Cout(n1_bit_alu_6_cout));
  _1_bit_ALU u_1_bit_alu_7 (
    .A(A[6]), .B(B[6]), .CarryIn(n1_bit_alu_6_cout), .S1S0(ALU_Operation), .Result(Result[6]),
    .Cout(n1_bit_alu_7_cout));
  _1_bit_ALU u_1_bit_alu_8 (
    .A(A[7]), .B(B[7]), .CarryIn(n1_bit_alu_7_cout), .S1S0(ALU_Operation), .Result(Result[7]),
    .Cout(n1_bit_alu_8_cout));
  _1_bit_ALU u_1_bit_alu_9 (
    .A(A[8]), .B(B[8]), .CarryIn(n1_bit_alu_8_cout), .S1S0(ALU_Operation), .Result(Result[8]),
    .Cout(n1_bit_alu_9_cout));
  _1_bit_ALU u_1_bit_alu_10 (
    .A(A[9]), .B(B[9]), .CarryIn(n1_bit_alu_9_cout), .S1S0(ALU_Operation), .Result(Result[9]),
    .Cout(n1_bit_alu_10_cout));
  _1_bit_ALU u_1_bit_alu_11 (
    .A(A[10]), .B(B[10]), .CarryIn(n1_bit_alu_10_cout), .S1S0(ALU_Operation), .Result(Result[10]),
    .Cout(n1_bit_alu_11_cout));
  _1_bit_ALU u_1_bit_alu_12 (
    .A(A[11]), .B(B[11]), .CarryIn(n1_bit_alu_11_cout), .S1S0(ALU_Operation), .Result(Result[11]),
    .Cout(n1_bit_alu_12_cout));
  _1_bit_ALU u_1_bit_alu_13 (
    .A(A[12]), .B(B[12]), .CarryIn(n1_bit_alu_12_cout), .S1S0(ALU_Operation), .Result(Result[12]),
    .Cout(n1_bit_alu_13_cout));
  _1_bit_ALU u_1_bit_alu_14 (
    .A(A[13]), .B(B[13]), .CarryIn(n1_bit_alu_13_cout), .S1S0(ALU_Operation), .Result(Result[13]),
    .Cout(n1_bit_alu_14_cout));
  _1_bit_ALU u_1_bit_alu_15 (
    .A(A[14]), .B(B[14]), .CarryIn(n1_bit_alu_14_cout), .S1S0(ALU_Operation), .Result(Result[14]),
    .Cout(n1_bit_alu_15_cout));
  _1_bit_ALU u_1_bit_alu_16 (
    .A(A[15]), .B(B[15]), .CarryIn(n1_bit_alu_15_cout), .S1S0(ALU_Operation), .Result(Result[15]),
    .Cout(n1_bit_alu_16_cout));
  _1_bit_ALU u_1_bit_alu_17 (
    .A(A[16]), .B(B[16]), .CarryIn(n1_bit_alu_16_cout), .S1S0(ALU_Operation), .Result(Result[16]),
    .Cout(n1_bit_alu_17_cout));
  _1_bit_ALU u_1_bit_alu_18 (
    .A(A[17]), .B(B[17]), .CarryIn(n1_bit_alu_17_cout), .S1S0(ALU_Operation), .Result(Result[17]),
    .Cout(n1_bit_alu_18_cout));
  _1_bit_ALU u_1_bit_alu_19 (
    .A(A[18]), .B(B[18]), .CarryIn(n1_bit_alu_18_cout), .S1S0(ALU_Operation), .Result(Result[18]),
    .Cout(n1_bit_alu_19_cout));
  _1_bit_ALU u_1_bit_alu_20 (
    .A(A[19]), .B(B[19]), .CarryIn(n1_bit_alu_19_cout), .S1S0(ALU_Operation), .Result(Result[19]),
    .Cout(n1_bit_alu_20_cout));
  _1_bit_ALU u_1_bit_alu_21 (
    .A(A[20]), .B(B[20]), .CarryIn(n1_bit_alu_20_cout), .S1S0(ALU_Operation), .Result(Result[20]),
    .Cout(n1_bit_alu_21_cout));
  _1_bit_ALU u_1_bit_alu_22 (
    .A(A[21]), .B(B[21]), .CarryIn(n1_bit_alu_21_cout), .S1S0(ALU_Operation), .Result(Result[21]),
    .Cout(n1_bit_alu_22_cout));
  _1_bit_ALU u_1_bit_alu_23 (
    .A(A[22]), .B(B[22]), .CarryIn(n1_bit_alu_22_cout), .S1S0(ALU_Operation), .Result(Result[22]),
    .Cout(n1_bit_alu_23_cout));
  _1_bit_ALU u_1_bit_alu_24 (
    .A(A[23]), .B(B[23]), .CarryIn(n1_bit_alu_23_cout), .S1S0(ALU_Operation), .Result(Result[23]),
    .Cout(n1_bit_alu_24_cout));
  _1_bit_ALU u_1_bit_alu_25 (
    .A(A[24]), .B(B[24]), .CarryIn(n1_bit_alu_24_cout), .S1S0(ALU_Operation), .Result(Result[24]),
    .Cout(n1_bit_alu_25_cout));
  _1_bit_ALU u_1_bit_alu_26 (
    .A(A[25]), .B(B[25]), .CarryIn(n1_bit_alu_25_cout), .S1S0(ALU_Operation), .Result(Result[25]),
    .Cout(n1_bit_alu_26_cout));
  _1_bit_ALU u_1_bit_alu_27 (
    .A(A[26]), .B(B[26]), .CarryIn(n1_bit_alu_26_cout), .S1S0(ALU_Operation), .Result(Result[26]),
    .Cout(n1_bit_alu_27_cout));
  _1_bit_ALU u_1_bit_alu_28 (
    .A(A[27]), .B(B[27]), .CarryIn(n1_bit_alu_27_cout), .S1S0(ALU_Operation), .Result(Result[27]),
    .Cout(n1_bit_alu_28_cout));
  _1_bit_ALU u_1_bit_alu_29 (
    .A(A[28]), .B(B[28]), .CarryIn(n1_bit_alu_28_cout), .S1S0(ALU_Operation), .Result(Result[28]),
    .Cout(n1_bit_alu_29_cout));
  _1_bit_ALU u_1_bit_alu_30 (
    .A(A[29]), .B(B[29]), .CarryIn(n1_bit_alu_29_cout), .S1S0(ALU_Operation), .Result(Result[29]),
    .Cout(n1_bit_alu_30_cout));
  _1_bit_ALU u_1_bit_alu_31 (
    .A(A[30]), .B(B[30]), .CarryIn(n1_bit_alu_30_cout), .S1S0(ALU_Operation), .Result(Result[30]),
    .Cout(n1_bit_alu_31_cout));
  _1_bit_ALU u_1_bit_alu_32 (
    .A(A[31]), .B(B[31]), .CarryIn(n1_bit_alu_31_cout), .S1S0(ALU_Operation), .Result(Result[31]),
    .Cout(out_9));
  and and_2 (Overflow, A[31], B[31]);
  nor nor_1 (Zero, Result[0], Result[1], Result[2], Result[3], Result[4], Result[5], Result[6], Result[7], Result[8], Result[9], Result[10], Result[11], Result[12], Result[13], Result[14], Result[15], Result[16], Result[17], Result[18], Result[19], Result[20], Result[21], Result[22], Result[23], Result[24], Result[25], Result[26], Result[27], Result[28], Result[29], Result[30], Result[31]);

  // Other names for the same wires on the sheet: ALU_OP[1:0] = ALU_Operation; R0 = Result[0]; R1 = Result[1];
  //   R2 = Result[2]; R3 = Result[3]; R4 = Result[4]; R5 = Result[5]; R6 = Result[6]; R7 = Result[7]; R8 = Result[8];
  //   R9 = Result[9]; R10 = Result[10]; R11 = Result[11]; R12 = Result[12]; R13 = Result[13]; R14 = Result[14];
  //   R15 = Result[15]; R16 = Result[16]; R17 = Result[17]; R18 = Result[18]; R19 = Result[19]; R20 = Result[20];
  //   R21 = Result[21]; R22 = Result[22]; R23 = Result[23]; R24 = Result[24]; R25 = Result[25]; R26 = Result[26];
  //   R27 = Result[27]; R28 = Result[28]; R29 = Result[29]; R30 = Result[30]; R31 = Result[31]
endmodule

module _32_bit_RF (
  input  [31:0] Data_In,
  input  Reg_Write,
  input  [4:0] Read_Address_1,
  input  [4:0] Write_Address,
  input  [4:0] Read_Address_2,
  input  in_6,
  output [31:0] Data_Out_1,
  output [31:0] Data_Out_2
);

  wire and_1_out, and_2_out, and_3_out, and_4_out, and_5_out, and_6_out, and_7_out, and_8_out, and_9_out,
       and_10_out, and_11_out, and_12_out, and_13_out, and_14_out, and_15_out, and_16_out, and_17_out,
       and_18_out, and_19_out, and_20_out, and_21_out, and_22_out, and_23_out, and_24_out, and_25_out,
       and_26_out, and_27_out, and_28_out, and_29_out, and_30_out, and_31_out, and_32_out, decoder_1_out0,
       decoder_1_out1, decoder_1_out2, decoder_1_out3, decoder_1_out4, decoder_1_out5, decoder_1_out6,
       decoder_1_out7, decoder_1_out8, decoder_1_out9, decoder_1_out10, decoder_1_out11, decoder_1_out12,
       decoder_1_out13, decoder_1_out14, decoder_1_out15, decoder_1_out16, decoder_1_out17, decoder_1_out18,
       decoder_1_out19, decoder_1_out20, decoder_1_out21, decoder_1_out22, decoder_1_out23, decoder_1_out24,
       decoder_1_out25, decoder_1_out26, decoder_1_out27, decoder_1_out28, decoder_1_out29, decoder_1_out30,
       decoder_1_out31;
  wire [31:0] register_1_q, register_2_q, register_3_q, register_4_q, register_5_q, register_6_q,
       register_7_q, register_8_q, register_9_q, register_10_q, register_11_q, register_12_q, register_13_q,
       register_14_q, register_15_q, register_16_q, register_17_q, register_18_q, register_19_q,
       register_20_q, register_21_q, register_22_q, register_23_q, register_24_q, register_25_q,
       register_26_q, register_27_q, register_28_q, register_29_q, register_30_q, register_31_q,
       register_32_q;

  Decoder #(.select(5), .enable("false")) decoder_1 (
    .out0(decoder_1_out0), .out1(decoder_1_out1), .out2(decoder_1_out2), .out3(decoder_1_out3),
    .out4(decoder_1_out4), .out5(decoder_1_out5), .out6(decoder_1_out6), .out7(decoder_1_out7),
    .out8(decoder_1_out8), .out9(decoder_1_out9), .out10(decoder_1_out10), .out11(decoder_1_out11),
    .out12(decoder_1_out12), .out13(decoder_1_out13), .out14(decoder_1_out14), .out15(decoder_1_out15),
    .out16(decoder_1_out16), .out17(decoder_1_out17), .out18(decoder_1_out18), .out19(decoder_1_out19),
    .out20(decoder_1_out20), .out21(decoder_1_out21), .out22(decoder_1_out22), .out23(decoder_1_out23),
    .out24(decoder_1_out24), .out25(decoder_1_out25), .out26(decoder_1_out26), .out27(decoder_1_out27),
    .out28(decoder_1_out28), .out29(decoder_1_out29), .out30(decoder_1_out30), .out31(decoder_1_out31),
    .sel(Write_Address));
  and and_1 (and_1_out, decoder_1_out0, Reg_Write);
  and and_2 (and_2_out, decoder_1_out1, Reg_Write);
  and and_3 (and_3_out, decoder_1_out2, Reg_Write);
  and and_4 (and_4_out, decoder_1_out3, Reg_Write);
  and and_5 (and_5_out, decoder_1_out4, Reg_Write);
  and and_6 (and_6_out, decoder_1_out5, Reg_Write);
  and and_7 (and_7_out, decoder_1_out6, Reg_Write);
  and and_8 (and_8_out, decoder_1_out7, Reg_Write);
  and and_9 (and_9_out, decoder_1_out8, Reg_Write);
  and and_10 (and_10_out, decoder_1_out9, Reg_Write);
  and and_11 (and_11_out, decoder_1_out10, Reg_Write);
  and and_12 (and_12_out, decoder_1_out11, Reg_Write);
  and and_13 (and_13_out, decoder_1_out12, Reg_Write);
  and and_14 (and_14_out, decoder_1_out13, Reg_Write);
  and and_15 (and_15_out, decoder_1_out14, Reg_Write);
  and and_16 (and_16_out, decoder_1_out15, Reg_Write);
  and and_17 (and_17_out, decoder_1_out16, Reg_Write);
  and and_18 (and_18_out, decoder_1_out17, Reg_Write);
  and and_19 (and_19_out, decoder_1_out18, Reg_Write);
  and and_20 (and_20_out, decoder_1_out19, Reg_Write);
  and and_21 (and_21_out, decoder_1_out20, Reg_Write);
  and and_22 (and_22_out, decoder_1_out21, Reg_Write);
  and and_23 (and_23_out, decoder_1_out22, Reg_Write);
  and and_24 (and_24_out, decoder_1_out23, Reg_Write);
  and and_25 (and_25_out, decoder_1_out24, Reg_Write);
  and and_26 (and_26_out, decoder_1_out25, Reg_Write);
  and and_27 (and_27_out, decoder_1_out26, Reg_Write);
  and and_28 (and_28_out, decoder_1_out27, Reg_Write);
  and and_29 (and_29_out, decoder_1_out28, Reg_Write);
  and and_30 (and_30_out, decoder_1_out29, Reg_Write);
  and and_31 (and_31_out, decoder_1_out30, Reg_Write);
  and and_32 (and_32_out, decoder_1_out31, Reg_Write);
  Register #(.width(32)) register_1 (.D(Data_In), .en(and_1_out), .Q(register_1_q), .clk(in_6));  // open: clr
  Register #(.width(32)) register_2 (.D(Data_In), .en(and_2_out), .Q(register_2_q), .clk(in_6));  // open: clr
  Register #(.width(32)) register_3 (.D(Data_In), .en(and_3_out), .Q(register_3_q), .clk(in_6));  // open: clr
  Register #(.width(32)) register_4 (.D(Data_In), .en(and_4_out), .Q(register_4_q), .clk(in_6));  // open: clr
  Register #(.width(32)) register_5 (.D(Data_In), .en(and_5_out), .Q(register_5_q), .clk(in_6));  // open: clr
  Register #(.width(32)) register_6 (.D(Data_In), .en(and_6_out), .Q(register_6_q), .clk(in_6));  // open: clr
  Register #(.width(32)) register_7 (.D(Data_In), .en(and_7_out), .Q(register_7_q), .clk(in_6));  // open: clr
  Register #(.width(32)) register_8 (.D(Data_In), .en(and_8_out), .Q(register_8_q), .clk(in_6));  // open: clr
  Register #(.width(32)) register_9 (.D(Data_In), .en(and_9_out), .Q(register_9_q), .clk(in_6));  // open: clr
  Register #(.width(32)) register_10 (.D(Data_In), .en(and_10_out), .Q(register_10_q), .clk(in_6));  // open: clr
  Register #(.width(32)) register_11 (.D(Data_In), .en(and_11_out), .Q(register_11_q), .clk(in_6));  // open: clr
  Register #(.width(32)) register_12 (.D(Data_In), .en(and_12_out), .Q(register_12_q), .clk(in_6));  // open: clr
  Register #(.width(32)) register_13 (.D(Data_In), .en(and_13_out), .Q(register_13_q), .clk(in_6));  // open: clr
  Register #(.width(32)) register_14 (.D(Data_In), .en(and_14_out), .Q(register_14_q), .clk(in_6));  // open: clr
  Register #(.width(32)) register_15 (.D(Data_In), .en(and_15_out), .Q(register_15_q), .clk(in_6));  // open: clr
  Register #(.width(32)) register_16 (.D(Data_In), .en(and_16_out), .Q(register_16_q), .clk(in_6));  // open: clr
  Register #(.width(32)) register_17 (.D(Data_In), .en(and_17_out), .Q(register_17_q), .clk(in_6));  // open: clr
  Register #(.width(32)) register_18 (.D(Data_In), .en(and_18_out), .Q(register_18_q), .clk(in_6));  // open: clr
  Register #(.width(32)) register_19 (.D(Data_In), .en(and_19_out), .Q(register_19_q), .clk(in_6));  // open: clr
  Register #(.width(32)) register_20 (.D(Data_In), .en(and_20_out), .Q(register_20_q), .clk(in_6));  // open: clr
  Register #(.width(32)) register_21 (.D(Data_In), .en(and_21_out), .Q(register_21_q), .clk(in_6));  // open: clr
  Register #(.width(32)) register_22 (.D(Data_In), .en(and_22_out), .Q(register_22_q), .clk(in_6));  // open: clr
  Register #(.width(32)) register_23 (.D(Data_In), .en(and_23_out), .Q(register_23_q), .clk(in_6));  // open: clr
  Register #(.width(32)) register_24 (.D(Data_In), .en(and_24_out), .Q(register_24_q), .clk(in_6));  // open: clr
  Register #(.width(32)) register_25 (.D(Data_In), .en(and_25_out), .Q(register_25_q), .clk(in_6));  // open: clr
  Register #(.width(32)) register_26 (.D(Data_In), .en(and_26_out), .Q(register_26_q), .clk(in_6));  // open: clr
  Register #(.width(32)) register_27 (.D(Data_In), .en(and_27_out), .Q(register_27_q), .clk(in_6));  // open: clr
  Register #(.width(32)) register_28 (.D(Data_In), .en(and_28_out), .Q(register_28_q), .clk(in_6));  // open: clr
  Register #(.width(32)) register_29 (.D(Data_In), .en(and_29_out), .Q(register_29_q), .clk(in_6));  // open: clr
  Register #(.width(32)) register_30 (.D(Data_In), .en(and_30_out), .Q(register_30_q), .clk(in_6));  // open: clr
  Register #(.width(32)) register_31 (.D(Data_In), .en(and_31_out), .Q(register_31_q), .clk(in_6));  // open: clr
  Register #(.width(32)) register_32 (.D(Data_In), .en(and_32_out), .Q(register_32_q), .clk(in_6));  // open: clr
  Multiplexer #(.select(5), .width(32), .enable("false")) multiplexer_1 (
    .in0(register_1_q), .in1(register_2_q), .in2(register_3_q), .in3(register_4_q), .in4(register_5_q),
    .in5(register_6_q), .in6(register_7_q), .in7(register_8_q), .in8(register_9_q), .in9(register_10_q),
    .in10(register_11_q), .in11(register_12_q), .in12(register_13_q), .in13(register_14_q),
    .in14(register_15_q), .in15(register_16_q), .in16(register_17_q), .in17(register_18_q),
    .in18(register_19_q), .in19(register_20_q), .in20(register_21_q), .in21(register_22_q),
    .in22(register_23_q), .in23(register_24_q), .in24(register_25_q), .in25(register_26_q),
    .in26(register_27_q), .in27(register_28_q), .in28(register_29_q), .in29(register_30_q),
    .in30(register_31_q), .in31(register_32_q), .out(Data_Out_1), .sel(Read_Address_1));
  Multiplexer #(.select(5), .width(32), .enable("false")) multiplexer_2 (
    .in0(register_1_q), .in1(register_2_q), .in2(register_3_q), .in3(register_4_q), .in4(register_5_q),
    .in5(register_6_q), .in6(register_7_q), .in7(register_8_q), .in8(register_9_q), .in9(register_10_q),
    .in10(register_11_q), .in11(register_12_q), .in12(register_13_q), .in13(register_14_q),
    .in14(register_15_q), .in15(register_16_q), .in16(register_17_q), .in17(register_18_q),
    .in18(register_19_q), .in19(register_20_q), .in20(register_21_q), .in21(register_22_q),
    .in22(register_23_q), .in23(register_24_q), .in24(register_25_q), .in25(register_26_q),
    .in26(register_27_q), .in27(register_28_q), .in28(register_29_q), .in29(register_30_q),
    .in30(register_31_q), .in31(register_32_q), .out(Data_Out_2), .sel(Read_Address_2));
endmodule
